# Fritzing sketch Steering Wheel Board (saved by Fritzing 0.9.3b)
perfboards: 1

parts:
  J1 = female pin header, 11 pins [form="♀ (female)"]
  J3 = female pin header, 3 pins [form="♀ (female)"]
  J5 = female pin header, 11 pins [form="♀ (female)"]
  S2 = Toggle Switch [package=THT]
  S3 = Toggle Switch [package=THT]
  S4 = Toggle Switch [package=THT]
  S5 = Toggle Switch [package=THT]
  S6 = Toggle Switch [package=THT]
  CD4048B1 = CD4048B [part_number=CD4048B package="DIP (Dual Inline) [THT]"]
  J6 = Power Jack [package=power_jack_smd]
  R3 = Resistor [tolerance=±5% resistance=220 package="0805 [SMD]"]
  J1_2 = female pin header, 6 pins [form="♀ (female)"]
  J2 = female pin header, 3 pins [form="♀ (female)"]
  J4 = female pin header, 7 pins [form="♀ (female)"]
  R5 = Resistor [tolerance=±5% resistance=220 package="0805 [SMD]"]
  switch1 = RM-series Subminiature Rotary Switch
  switch2 = RM-series Subminiature Rotary Switch

nets:
  N1: J1.pin1, CD4048B1.C
  N2: J1.pin2, CD4048B1.Ka
  N3: J1.pin3, CD4048B1.E
  N4: J1.pin4, CD4048B1.G
  N5: J1.pin5, CD4048B1.Kd
  VSS: J1.pin6, J1.pin7, J1.pin9, J1.pin10, J3.pin1, CD4048B1.VSS, J6.GND, J2.pin2
  N6: J1.pin8, J1.pin11, R3.Pin_0, R5.Pin_1
  N7: J3.pin2, CD4048B1.J, R3.Pin_1
  N8: J3.pin3, J1_2.pin6
  N9: J5.pin1, switch2.3
  N10: J5.pin2, switch2.2
  N11: J5.pin3, switch2.1
  N12: J5.pin4, switch1.3
  N13: J5.pin5, switch1.2
  N14: J5.pin6, switch1.1
  N15: J5.pin7, S2.COM
  N16: J5.pin8, S3.COM
  N17: J5.pin9, S4.COM
  N18: J5.pin10, S5.COM
  N19: J5.pin11, S6.COM
  N20: S2.L2, S3.L2, S4.L2, S5.L2, S6.L2, J2.pin1, J4.pin1, J4.pin2, J4.pin3, J4.pin4, J4.pin5, J4.pin6, J4.pin7, switch1.0, switch2.0
  N21: CD4048B1.H, J1_2.pin1
  N22: CD4048B1.F, J1_2.pin2
  N23: CD4048B1.Kb, J1_2.pin3
  N24: CD4048B1.Kc, J1_2.pin4
  N25: CD4048B1.D, J1_2.pin5
  N26: J6.GNDBREAK, J2.pin3, R5.Pin_0
