# Fritzing sketch Steering Wheel Internal Test v1 (saved by Fritzing 0.9.3b)
perfboards: 1

parts:
  Part2 = Arduino ProtoShield
  J1 = Power Jack [package=power_jack_pth_lock]  # not connected
  Part1 = Arduino Nano (Rev3.0)

nets:
  N1: Part2.RESET, Part1.RESET
  3.3V: Part2.3.3V, Part1.3V3
  5V: Part2.5V, Part1.5V
  GND: Part2.GND, Part1.GND
  N2: Part2.D2, Part1.D2
  N3: Part2.D3, Part1.D3
  N4: Part2.D9, Part1.D9
  N5: Part2.D10, Part1.D10
  N6: Part2.D11, Part1.D11/MOSI
  N7: Part2.D12, Part1.D12/MISO
  N8: Part2.D13, Part1.D13/SCK
  N9: Part2.AREF, Part1.AREF
